// Logisim project LogisimCode.circ as structural Verilog: 7 circuits, main circuit main
module main (
  input  in_1,
  input  in_2,
  input  in_3,
  input  in_4,
  input  in_5,
  input  in_6,
  input  in_7,
  input  in_8,
  input  in_9
);

  wire ryn2_1_a1, ryn2_1_b1, ryn2_1_c1, ryn2_1_d1, ryn2_1_e1, ryn2_1_f1, ryn2_1_g1, ryn2_1_out_17,
       ryn2_1_out_18, ryn2_1_out_19, ryn2_1_out_20, ryn2_1_out_21, ryn2_1_out_22, ryn2_1_out_23, ryn6_1_a_2,
       ryn6_1_b_2, ryn6_1_c_2, ryn6_1_d_2, ryn6_1_e_2, ryn6_1_f_2, ryn6_1_g, ryn6_1_h_2, ryn6_1_i_2, ryn6_1_j;

  LED led_1 (.in(ryn6_1_a_2));
  LED led_2 (.in(ryn6_1_c_2));
  LED led_3 (.in(ryn6_1_f_2));
  LED led_4 (.in(ryn6_1_b_2));
  LED led_5 (.in(ryn6_1_g));
  LED led_6 (.in(ryn6_1_d_2));
  LED led_7 (.in(ryn6_1_e_2));
  LED led_8 (.in(ryn6_1_h_2));
  LED led_9 (.in(ryn6_1_i_2));
  LED led_10 (.in(ryn6_1_j));
  ryn2 ryn2_1 (
    .A(in_1), .B(in_3), .C(in_2), .D(in_4), .E(in_6), .F(in_5), .G(in_8), .H(in_9), .I(in_7), .a1(ryn2_1_a1),
    .b1(ryn2_1_b1), .c1(ryn2_1_c1), .d1(ryn2_1_d1), .e1(ryn2_1_e1), .f1(ryn2_1_f1), .g1(ryn2_1_g1),
    .out_17(ryn2_1_out_17), .out_18(ryn2_1_out_18), .out_19(ryn2_1_out_19), .out_20(ryn2_1_out_20),
    .out_21(ryn2_1_out_21), .out_22(ryn2_1_out_22), .out_23(ryn2_1_out_23));
  ryn6 ryn6_1 (
    .A(in_1), .B(in_3), .C(in_2), .D(in_4), .E(in_6), .F(in_5), .R(in_8), .H(in_9), .I(in_7),
    .a_2(ryn6_1_a_2), .b_2(ryn6_1_b_2), .c_2(ryn6_1_c_2), .d_2(ryn6_1_d_2), .e_2(ryn6_1_e_2),
    .f_2(ryn6_1_f_2), .g(ryn6_1_g), .h_2(ryn6_1_h_2), .i_2(ryn6_1_i_2), .j(ryn6_1_j));
  _7_Segment_Display u_7_segment_display_1 (
    .g(ryn2_1_d1), .f(ryn2_1_c1), .a(ryn2_1_b1), .b(ryn2_1_a1), .e(ryn2_1_e1), .d(ryn2_1_f1), .c(ryn2_1_g1));  // open: dp
  _7_Segment_Display u_7_segment_display_2 (
    .g(ryn2_1_out_20), .f(ryn2_1_out_19), .a(ryn2_1_out_18), .b(ryn2_1_out_17), .e(ryn2_1_out_21),
    .d(ryn2_1_out_22), .c(ryn2_1_out_23));  // open: dp

  // Notes on the sheet:
  //   Motion in Y Coordinate
  //   Motion in X Coordinate
endmodule

module ryn (
  input  A,
  input  B,
  input  C,
  input  D,
  input  E,
  input  F,
  input  G,
  input  H,
  input  I,
  output a1,
  output b1,
  output c1,
  output d1,
  output e1,
  output f1,
  output g1
);

  wire and_1_out, and_2_out, and_3_out, and_4_out, and_5_out, and_6_out, and_7_out, and_8_out, and_9_out,
       and_10_out, and_11_out, and_12_out, not_1_out, not_2_out, not_3_out, not_4_out, not_5_out, not_6_out,
       not_7_out, not_8_out, not_9_out, not_10_out, not_11_out, not_12_out, not_13_out, not_14_out,
       not_15_out, not_16_out, not_17_out, not_18_out, not_19_out, not_20_out, not_21_out, not_22_out,
       not_23_out, not_24_out, not_25_out, not_26_out, not_27_out, not_28_out, not_29_out, not_30_out,
       not_31_out, not_32_out, not_33_out, not_34_out, not_35_out, not_36_out, not_37_out, not_38_out,
       not_39_out, not_40_out, not_41_out, not_42_out, not_43_out, not_44_out, not_45_out;

  or or_1 (a1, I, H, G, F, E, D, C, B, A);
  not not_1 (not_1_out, D);
  not not_2 (not_2_out, E);
  not not_3 (not_3_out, F);
  not not_4 (not_4_out, D);
  not not_5 (not_5_out, E);
  not not_6 (not_6_out, F);
  not not_7 (not_7_out, D);
  not not_8 (not_8_out, E);
  not not_9 (not_9_out, F);
  or or_2 (c1, C, B, A);
  not not_10 (not_10_out, A);
  not not_11 (not_11_out, B);
  not not_12 (not_12_out, C);
  not not_13 (not_13_out, D);
  not not_14 (not_14_out, E);
  not not_15 (not_15_out, F);
  not not_16 (not_16_out, A);
  not not_17 (not_17_out, B);
  not not_18 (not_18_out, C);
  not not_19 (not_19_out, D);
  not not_20 (not_20_out, E);
  not not_21 (not_21_out, F);
  not not_22 (not_22_out, A);
  not not_23 (not_23_out, B);
  not not_24 (not_24_out, C);
  not not_25 (not_25_out, D);
  not not_26 (not_26_out, E);
  not not_27 (not_27_out, F);
  not not_28 (not_28_out, D);
  not not_29 (not_29_out, E);
  not not_30 (not_30_out, F);
  not not_31 (not_31_out, D);
  not not_32 (not_32_out, E);
  not not_33 (not_33_out, F);
  not not_34 (not_34_out, D);
  not not_35 (not_35_out, E);
  not not_36 (not_36_out, F);
  not not_37 (not_37_out, D);
  not not_38 (not_38_out, E);
  not not_39 (not_39_out, F);
  not not_40 (not_40_out, D);
  not not_41 (not_41_out, E);
  not not_42 (not_42_out, F);
  not not_43 (not_43_out, D);
  not not_44 (not_44_out, E);
  not not_45 (not_45_out, F);
  or or_3 (g1, F, E, D, C, B, A);
  and and_1 (and_1_out, not_1_out, not_2_out, not_3_out, I);
  and and_2 (and_2_out, not_4_out, not_5_out, not_6_out, H);
  and and_3 (and_3_out, not_7_out, not_8_out, not_9_out, G);
  and and_4 (and_4_out, not_10_out, not_11_out, not_12_out, not_13_out, not_14_out, not_15_out, I);
  and and_5 (and_5_out, not_16_out, not_17_out, not_18_out, not_19_out, not_20_out, not_21_out, H);
  and and_6 (and_6_out, not_22_out, not_23_out, not_24_out, not_25_out, not_26_out, not_27_out, G);
  and and_7 (and_7_out, not_28_out, not_29_out, not_30_out, I);
  and and_8 (and_8_out, not_31_out, not_32_out, not_33_out, H);
  and and_9 (and_9_out, not_34_out, not_35_out, not_36_out, G);
  and and_10 (and_10_out, not_37_out, not_38_out, not_39_out, I);
  and and_11 (and_11_out, not_40_out, not_41_out, not_42_out, H);
  and and_12 (and_12_out, not_43_out, not_44_out, not_45_out, G);
  or or_4 (b1, and_1_out, and_2_out, and_3_out, C, B, A);
  or or_5 (d1, and_4_out, and_5_out, and_6_out);
  or or_6 (e1, and_7_out, and_8_out, and_9_out, C, B, A);
  or or_7 (f1, and_10_out, and_11_out, and_12_out, C, B, A);
endmodule

module ryn2 (
  input  A,
  input  B,
  input  C,
  input  D,
  input  E,
  input  F,
  input  G,
  input  H,
  input  I,
  output a1,
  output b1,
  output c1,
  output d1,
  output e1,
  output f1,
  output g1,
  output out_17,
  output out_18,
  output out_19,
  output out_20,
  output out_21,
  output out_22,
  output out_23
);

  wire and_1_out, and_2_out, and_3_out, and_4_out, and_5_out, and_6_out, and_7_out, and_8_out, and_9_out,
       and_10_out, and_11_out, and_12_out, not_1_out, not_2_out, not_3_out, not_4_out, not_5_out, not_6_out,
       not_7_out, not_8_out, not_9_out, not_10_out, not_11_out, not_12_out, not_13_out, not_14_out,
       not_15_out, not_16_out, not_17_out, not_18_out, not_19_out, not_20_out, not_21_out, not_22_out,
       not_23_out, not_24_out, not_25_out, not_26_out, not_27_out, not_28_out, not_29_out, not_30_out,
       not_31_out, not_32_out, not_33_out, not_34_out, not_35_out, not_36_out, not_37_out, not_38_out,
       not_39_out, not_40_out, not_41_out, not_42_out, not_43_out, not_44_out, not_45_out;

  or or_1 (a1, I, H, G, F, E, D, C, B, A);
  not not_1 (not_1_out, D);
  not not_2 (not_2_out, E);
  not not_3 (not_3_out, F);
  not not_4 (not_4_out, D);
  not not_5 (not_5_out, E);
  not not_6 (not_6_out, F);
  not not_7 (not_7_out, D);
  not not_8 (not_8_out, E);
  not not_9 (not_9_out, F);
  or or_2 (c1, C, B, A);
  not not_10 (not_10_out, A);
  not not_11 (not_11_out, B);
  not not_12 (not_12_out, C);
  not not_13 (not_13_out, D);
  not not_14 (not_14_out, E);
  not not_15 (not_15_out, F);
  not not_16 (not_16_out, A);
  not not_17 (not_17_out, B);
  not not_18 (not_18_out, C);
  not not_19 (not_19_out, D);
  not not_20 (not_20_out, E);
  not not_21 (not_21_out, F);
  not not_22 (not_22_out, A);
  not not_23 (not_23_out, B);
  not not_24 (not_24_out, C);
  not not_25 (not_25_out, D);
  not not_26 (not_26_out, E);
  not not_27 (not_27_out, F);
  not not_28 (not_28_out, D);
  not not_29 (not_29_out, E);
  not not_30 (not_30_out, F);
  not not_31 (not_31_out, D);
  not not_32 (not_32_out, E);
  not not_33 (not_33_out, F);
  not not_34 (not_34_out, D);
  not not_35 (not_35_out, E);
  not not_36 (not_36_out, F);
  not not_37 (not_37_out, D);
  not not_38 (not_38_out, E);
  not not_39 (not_39_out, F);
  not not_40 (not_40_out, D);
  not not_41 (not_41_out, E);
  not not_42 (not_42_out, F);
  not not_43 (not_43_out, D);
  not not_44 (not_44_out, E);
  not not_45 (not_45_out, F);
  or or_3 (g1, F, E, D, C, B, A);
  ryn ryn_1 (
    .A(A), .B(D), .C(G), .D(B), .E(E), .F(H), .G(C), .H(F), .I(I), .a1(out_17), .b1(out_18), .c1(out_19),
    .d1(out_20), .e1(out_21), .f1(out_22), .g1(out_23));
  and and_1 (and_1_out, not_1_out, not_2_out, not_3_out, I);
  and and_2 (and_2_out, not_4_out, not_5_out, not_6_out, H);
  and and_3 (and_3_out, not_7_out, not_8_out, not_9_out, G);
  and and_4 (and_4_out, not_10_out, not_11_out, not_12_out, not_13_out, not_14_out, not_15_out, I);
  and and_5 (and_5_out, not_16_out, not_17_out, not_18_out, not_19_out, not_20_out, not_21_out, H);
  and and_6 (and_6_out, not_22_out, not_23_out, not_24_out, not_25_out, not_26_out, not_27_out, G);
  and and_7 (and_7_out, not_28_out, not_29_out, not_30_out, I);
  and and_8 (and_8_out, not_31_out, not_32_out, not_33_out, H);
  and and_9 (and_9_out, not_34_out, not_35_out, not_36_out, G);
  and and_10 (and_10_out, not_37_out, not_38_out, not_39_out, I);
  and and_11 (and_11_out, not_40_out, not_41_out, not_42_out, H);
  and and_12 (and_12_out, not_43_out, not_44_out, not_45_out, G);
  or or_4 (b1, and_1_out, and_2_out, and_3_out, C, B, A);
  or or_5 (d1, and_4_out, and_5_out, and_6_out);
  or or_6 (e1, and_7_out, and_8_out, and_9_out, C, B, A);
  or or_7 (f1, and_10_out, and_11_out, and_12_out, C, B, A);
endmodule

module ryn3 (
  input  A,
  input  B,
  input  C,
  input  D,
  input  E,
  input  F,
  input  G,
  input  H,
  input  I,
  output a1,
  output b1,
  output c1,
  output d1,
  output e1,
  output f1,
  output g1
);

  wire not_1_out, not_2_out, not_3_out, not_4_out, not_5_out, not_6_out, not_7_out, not_8_out, not_9_out,
       not_10_out, not_11_out, not_12_out, not_13_out, not_14_out, not_15_out, not_16_out, not_17_out,
       not_18_out, not_19_out, not_20_out, not_21_out, not_22_out, not_23_out, not_24_out;

  not not_1 (not_1_out, D);
  not not_2 (not_2_out, E);
  not not_3 (not_3_out, F);
  not not_4 (not_4_out, D);
  not not_5 (not_5_out, E);
  not not_6 (not_6_out, F);
  not not_7 (not_7_out, G);
  not not_8 (not_8_out, H);
  not not_9 (not_9_out, I);
  not not_10 (not_10_out, A);
  not not_11 (not_11_out, B);
  not not_12 (not_12_out, C);
  not not_13 (not_13_out, D);
  not not_14 (not_14_out, E);
  not not_15 (not_15_out, F);
  not not_16 (not_16_out, D);
  not not_17 (not_17_out, E);
  not not_18 (not_18_out, F);
  not not_19 (not_19_out, D);
  not not_20 (not_20_out, E);
  not not_21 (not_21_out, F);
  not not_22 (not_22_out, G);
  not not_23 (not_23_out, H);
  not not_24 (not_24_out, I);
  and and_1 (b1, not_1_out, not_2_out, not_3_out);
  and and_2 (c1, not_4_out, not_5_out, not_6_out, not_7_out, not_8_out, not_9_out);
  and and_3 (d1, not_10_out, not_11_out, not_12_out, not_13_out, not_14_out, not_15_out);
  and and_4 (e1, not_16_out, not_17_out, not_18_out);
  and and_5 (f1, not_19_out, not_20_out, not_21_out);
  and and_6 (g1, not_22_out, not_23_out, not_24_out);

  assign a1 = 1'b1;
endmodule

module ryn4 (
  input  A,
  input  B,
  input  C,
  input  D,
  input  E,
  input  F,
  input  G,
  input  H,
  input  I,
  output a1,
  output b1,
  output c1,
  output d1,
  output e1,
  output f1,
  output g1,
  output out_17,
  output out_18,
  output out_19,
  output out_20,
  output out_21,
  output out_22,
  output out_23
);

  wire not_1_out, not_2_out, not_3_out, not_4_out, not_5_out, not_6_out, not_7_out, not_8_out, not_9_out,
       not_10_out, not_11_out, not_12_out, not_13_out, not_14_out, not_15_out, not_16_out, not_17_out,
       not_18_out, not_19_out, not_20_out, not_21_out, not_22_out, not_23_out, not_24_out;

  not not_1 (not_1_out, B);
  not not_2 (not_2_out, E);
  not not_3 (not_3_out, H);
  not not_4 (not_4_out, B);
  not not_5 (not_5_out, C);
  not not_6 (not_6_out, E);
  not not_7 (not_7_out, F);
  not not_8 (not_8_out, H);
  not not_9 (not_9_out, I);
  not not_10 (not_10_out, A);
  not not_11 (not_11_out, B);
  not not_12 (not_12_out, D);
  not not_13 (not_13_out, E);
  not not_14 (not_14_out, G);
  not not_15 (not_15_out, H);
  not not_16 (not_16_out, B);
  not not_17 (not_17_out, E);
  not not_18 (not_18_out, H);
  not not_19 (not_19_out, B);
  not not_20 (not_20_out, E);
  not not_21 (not_21_out, H);
  not not_22 (not_22_out, C);
  not not_23 (not_23_out, F);
  not not_24 (not_24_out, I);
  ryn3 ryn3_1 (
    .A(A), .B(B), .C(C), .D(D), .E(E), .F(F), .G(G), .H(H), .I(I), .a1(out_17), .b1(out_18), .c1(out_19),
    .d1(out_20), .e1(out_21), .f1(out_22), .g1(out_23));
  and and_1 (b1, not_1_out, not_2_out, not_3_out);
  and and_2 (c1, not_4_out, not_5_out, not_6_out, not_7_out, not_8_out, not_9_out);
  and and_3 (d1, not_10_out, not_11_out, not_12_out, not_13_out, not_14_out, not_15_out);
  and and_4 (e1, not_16_out, not_17_out, not_18_out);
  and and_5 (f1, not_19_out, not_20_out, not_21_out);
  and and_6 (g1, not_22_out, not_23_out, not_24_out);

  assign a1 = 1'b1;
endmodule

module ryn5 (
  input  in_1,
  input  in_2,
  input  in_3,
  input  in_4,
  input  in_5,
  input  in_6,
  input  in_7,
  input  in_8,
  input  in_9
);
endmodule

module ryn6 (
  input  A,
  input  B,
  input  C,
  input  D,
  input  E,
  input  F,
  input  R,
  input  H,
  input  I,
  output a_2,
  output b_2,
  output c_2,
  output d_2,
  output e_2,
  output f_2,
  output g,
  output h_2,
  output i_2,
  output j
);

  or or_1 (a_2, I, H, R, F, E, C, B);
  or or_2 (b_2, D, A);
  or or_3 (d_2, I, H, R, F, E);
  or or_4 (e_2, R, E, D, B, A);
  or or_5 (f_2, I, H, F, E, C, B);
  or or_6 (g, E, D, A);
  or or_7 (i_2, C, B);
  or or_8 (j, H, R, F, E, D, C, B, A);

  assign c_2 = A;
  assign h_2 = I;
endmodule
